// Logisim project 6651071022_LAB2_1.circ as structural Verilog: 1 circuit, main circuit main
module main (
  input  EN,
  input  A2,
  input  A1,
  input  A0,
  output Y0,
  output Y1,
  output Y2,
  output Y3,
  output Y4,
  output Y5,
  output Y6,
  output Y7
);

  wire not_1_out, not_2_out, not_3_out;

  not not_1 (not_1_out, A2);
  not not_2 (not_2_out, A1);
  not not_3 (not_3_out, A0);
  and and_1 (Y0, EN, not_1_out, not_2_out, not_3_out);
  and and_2 (Y1, EN, not_1_out, not_2_out, A0);
  and and_3 (Y2, EN, not_1_out, A1, not_3_out);
  and and_4 (Y3, EN, not_1_out, A1, A0);
  and and_5 (Y4, EN, A2, not_2_out, not_3_out);
  and and_6 (Y5, EN, A2, not_2_out, A0);
  and and_7 (Y6, EN, A2, A1, not_3_out);
  and and_8 (Y7, EN, A2, A1, A0);

  // Notes on the sheet:
  //   Nguyễn Đức Hiền_6651071022
endmodule
