// Logisim project 6651071022_LAB2_3.circ as structural Verilog: 1 circuit, main circuit main
module main (
  input  A3,
  input  A2,
  input  B3,
  input  B2,
  input  A1,
  input  A0,
  input  B1,
  input  B0,
  output S3,
  output S2,
  output Cout,
  output S1,
  output S0
);

  wire and_1_out, and_2_out, and_3_out, and_4_out, and_5_out, and_6_out, and_7_out, and_8_out, or_2_out,
       or_3_out, or_4_out, xor_1_out, xor_2_out, xor_5_out, xor_6_out;

  xor xor_1 (xor_1_out, A3, B3);
  and and_1 (and_1_out, A3, B3);
  xor xor_2 (xor_2_out, A1, B1);
  and and_2 (and_2_out, A1, B1);
  xor xor_3 (S3, xor_1_out, or_3_out);
  and and_3 (and_3_out, xor_1_out, or_3_out);
  xor xor_4 (S1, xor_2_out, or_4_out);
  and and_4 (and_4_out, xor_2_out, or_4_out);
  or or_1 (Cout, and_1_out, and_3_out);
  or or_2 (or_2_out, and_2_out, and_4_out);
  xor xor_5 (xor_5_out, A2, B2);
  and and_5 (and_5_out, A2, B2);
  xor xor_6 (xor_6_out, A0, B0);
  and and_6 (and_6_out, A0, B0);
  xor xor_7 (S2, xor_5_out, or_2_out);
  and and_7 (and_7_out, xor_5_out, or_2_out);
  xor xor_8 (S0, xor_6_out, 1'b0);
  and and_8 (and_8_out, xor_6_out, 1'b0);
  or or_3 (or_3_out, and_5_out, and_7_out);
  or or_4 (or_4_out, and_6_out, and_8_out);

  // Notes on the sheet:
  //   Nguyễn Đức Hiền_6651071022
endmodule
