// Logisim project 6651071022_LAB2_5.circ as structural Verilog: 1 circuit, main circuit main
module main (
  input  A0,
  input  A1,
  input  A2,
  input  A3,
  input  B0,
  input  B1,
  input  B2,
  input  B3,
  output AGTB,
  output AEQB,
  output ALTB
);

  wire eq0, eq1, eq2, eq3, gt0, gt1, gt2, gt3, nb0, nb1, nb2, nb3, t0, t1, t2;

  xnor xnor_1 (eq0, A0, B0);
  xnor xnor_2 (eq1, A1, B1);
  xnor xnor_3 (eq2, A2, B2);
  xnor xnor_4 (eq3, A3, B3);
  not not_1 (nb0, B0);
  not not_2 (nb1, B1);
  not not_3 (nb2, B2);
  not not_4 (nb3, B3);
  and and_1 (gt0, A0, nb0);
  and and_2 (gt1, A1, nb1);
  and and_3 (gt2, A2, nb2);
  and and_4 (gt3, A3, nb3);
  and and_5 (t2, eq3, gt2);
  and and_6 (t1, eq3, eq2, gt1);
  and and_7 (t0, eq3, eq2, eq1, gt0);
  or or_1 (AGTB, gt3, t2, t1, t0);
  and and_8 (AEQB, eq3, eq2, eq1, eq0);
  nor nor_1 (ALTB, AGTB, AEQB);

  // Other names for the same wires on the sheet: EQ = AEQB; GT = AGTB; LT = ALTB

  // Notes on the sheet:
  //   Nguyễn Đức Hiền_6651071022
endmodule
