// Logisim project 6651071022_LAB2_6.circ as structural Verilog: 1 circuit, main circuit main
module main (
  input  RST,
  input  EN,
  output Q0,
  output Q1,
  output Q2,
  output Q3,
  output [3:0] Q
);

  wire a01, a012, clk, d0, d1, d2, d3;

  Clock clock_1 (.out(clk));
  not not_1 (d0, Q[0]);
  xor xor_1 (d1, Q[1], Q[0]);
  and and_1 (a01, Q[0], Q[1]);
  and and_2 (a012, Q[0], Q[1], Q[2]);
  D_Flip_Flop d_ff_1 (.clk(clk), .D(d0), .Q(Q[0]), .preset(1'b0), .en(EN), .reset(RST));  // open: Qn
  xor xor_2 (d2, Q[2], a01);
  xor xor_3 (d3, Q[3], a012);
  D_Flip_Flop d_ff_2 (.clk(clk), .D(d1), .Q(Q[1]), .preset(1'b0), .en(EN), .reset(RST));  // open: Qn
  D_Flip_Flop d_ff_3 (.clk(clk), .D(d2), .Q(Q[2]), .preset(1'b0), .en(EN), .reset(RST));  // open: Qn
  Hex_Digit_Display hex_digit_display_1 (.value(Q));  // open: dp
  D_Flip_Flop d_ff_4 (.clk(clk), .D(d3), .Q(Q[3]), .preset(1'b0), .en(EN), .reset(RST));  // open: Qn

  assign Q0 = Q[0];
  assign Q1 = Q[1];
  assign Q2 = Q[2];
  assign Q3 = Q[3];

  // Other names for the same wires on the sheet: qbus[3:0] = Q

  // Notes on the sheet:
  //   Nguyễn Đức Hiền_6651071022
endmodule
