// Logisim project 6651071022_LAB2_7.circ as structural Verilog: 1 circuit, main circuit main
module main (
  input  [2:0] Addr,
  input  [3:0] Din,
  input  Load,
  input  Clear,
  output [3:0] Dout
);

  wire clk;

  Clock clock_1 (.out(clk));
  RAM #(.addrWidth(3), .dataWidth(4), .bus("separate")) ram_1 (
    .addr(Addr), .din(Din), .data(Dout), .str(Load), .sel(1'b1), .clk(clk), .ld(1'b1), .clr(Clear));

  // Other names for the same wires on the sheet: clr = Clear; we = Load

  // Notes on the sheet:
  //   Nguyễn Đức Hiền_6651071022
endmodule
